// Digital circuit part_a.dig as structural Verilog
module part_a (
  input  in_0,
  input  in_1,
  input  in_2,
  output out_0
);

  wire or_1_out, or_2_out;

  or or_1 (or_1_out, in_0, ~in_1, ~in_2);  // Or
  or or_2 (or_2_out, ~in_0, ~in_1, in_2);  // Or
  and and_1 (out_0, or_1_out, or_2_out);
endmodule

/* Test case part_a_test:
in_0 in_1 in_2 out_0
0     0     0    1
0     0     1    1
0     1     0    1
0     1     1    0
1     0     0    1
1     0     1    1
1     1     0    0
1     1     1    1
*/
