// Digital circuit part_c.dig as structural Verilog
module part_c (
  input  in_0,
  input  in_1,
  input  in_2,
  output out_0
);

  wire nfet_1_s, nfet_3_s, pfet_1_d;

  PFET pfet_1 (.G(in_0), .S(1'b1), .D(pfet_1_d));
  NFET nfet_1 (.G(in_0), .D(pfet_1_d), .S(nfet_1_s));
  NFET nfet_2 (.G(in_1), .D(nfet_1_s), .S(1'b0));
  PFET pfet_2 (.G(in_1), .S(1'b1), .D(pfet_1_d));
  PFET pfet_3 (.G(pfet_1_d), .S(1'b1), .D(out_0));
  PFET pfet_4 (.G(in_2), .S(1'b1), .D(out_0));
  NFET nfet_3 (.G(pfet_1_d), .D(out_0), .S(nfet_3_s));
  NFET nfet_4 (.G(in_2), .D(nfet_3_s), .S(1'b0));
endmodule

/* Test case part_c_test:
in_0 in_1 in_2 out_0
 0    0     0    1
 0    0     1    0
 0    1     0    1
 0    1     1    0
 1    0     0    1
 1    0     1    0
 1    1     0    1
 1    1     1    1
*/
