// Digital circuit lab2_part2.dig as structural Verilog
module lab2_part2 (
  input  in0,
  input  in1,
  input  in2,
  input  in3,
  output seg_a,
  output seg_f,
  output seg_b,
  output seg_g,
  output seg_e,
  output seg_c,
  output seg_d,
  output seg_dp,
  output sign_a,
  output sign_f,
  output sign_b,
  output sign_g,
  output sign_e,
  output sign_c,
  output sign_d,
  output sign_dp
);

  wire and_1_out, and_2_out, and_3_out, and_4_out, and_5_out, and_6_out, and_7_out, and_8_out, and_9_out,
       and_10_out, and_11_out, and_12_out, and_13_out, and_16_out, and_17_out, and_18_out, and_19_out,
       and_20_out, and_21_out, nand_1_out, nor_1_out, nor_2_out, nor_3_out, nor_4_out, nor_5_out, nor_6_out,
       or_3_out, or_4_out, or_6_out, or_7_out, or_8_out, or_9_out, or_10_out;

  Seven_Seg seven_seg_1 (.a(1'b0), .b(1'b0), .c(1'b0), .d(1'b0), .e(1'b0), .f(1'b0), .g(in3), .dp(1'b0));
  Seven_Seg seven_seg_2 (.a(seg_a), .b(seg_b), .c(seg_c), .d(seg_d), .e(seg_e), .f(seg_f), .g(seg_g), .dp(1'b0));
  and and_1 (and_1_out, in3, ~in2);  // And
  and and_2 (and_2_out, in3, in0, ~in1);  // And
  and and_3 (and_3_out, in2, in0, ~in3);  // And
  and and_4 (and_4_out, in2, in0, ~in1);  // And
  and and_5 (and_5_out, in1, ~in3);  // And
  and and_6 (and_6_out, in1, ~in0);  // And
  nor nor_1 (nor_1_out, in0, in2);
  or or_1 (seg_a, and_1_out, and_2_out, and_3_out, and_4_out, and_5_out, and_6_out, nor_1_out);
  and and_7 (and_7_out, in3, ~in0);  // And
  and and_8 (and_8_out, in2, ~in1);  // And
  and and_9 (and_9_out, in1, ~in2);  // And
  and and_10 (and_10_out, in1, ~in0);  // And
  or or_2 (seg_g, and_7_out, and_8_out, and_9_out, and_10_out);
  and and_11 (and_11_out, in3, in2);
  nor nor_2 (nor_2_out, in3, in2);
  nor nor_3 (nor_3_out, in2, in1);
  and and_12 (and_12_out, in1, in0, ~in3);  // And
  and and_13 (and_13_out, in1, in0, in2);
  nor nor_4 (nor_4_out, in0, in1);
  or or_3 (or_3_out, in3, in2, ~in1, in0);  // Or
  or or_4 (or_4_out, ~in3, ~in2, ~in1, in0);  // Or
  and and_14 (seg_c, or_3_out, or_4_out);
  or or_5 (seg_b, and_11_out, nor_2_out, nor_3_out, and_12_out, and_13_out, nor_4_out);
  or or_6 (or_6_out, in3, in2, in1, ~in0);  // Or
  or or_7 (or_7_out, in3, ~in2, in1, in0);  // Or
  or or_8 (or_8_out, in3, ~in2, ~in1, ~in0);  // Or
  or or_9 (or_9_out, ~in3, in2, in1, ~in0);  // Or
  or or_10 (or_10_out, ~in3, ~in2, in1, in0);  // Or
  nand nand_1 (nand_1_out, in3, in2, in1, in0);
  and and_15 (seg_d, or_6_out, or_7_out, or_8_out, or_9_out, or_10_out, nand_1_out);
  and and_16 (and_16_out, ~in0, in1);  // And
  nor nor_5 (nor_5_out, in0, in2);
  or or_11 (seg_e, and_16_out, nor_5_out);
  and and_17 (and_17_out, ~in3, in2, ~in0);  // And
  and and_18 (and_18_out, ~in3, in2, ~in1);  // And
  and and_19 (and_19_out, in3, ~in2, in1);  // And
  and and_20 (and_20_out, in3, ~in2, ~in0);  // And
  and and_21 (and_21_out, ~in1, ~in0, in2);  // And
  nor nor_6 (nor_6_out, in1, in0, in3);
  or or_12 (seg_f, and_17_out, and_18_out, and_19_out, and_20_out, and_21_out, nor_6_out);

  assign seg_dp = 1'b0;
  assign sign_a = 1'b0;
  assign sign_b = 1'b0;
  assign sign_c = 1'b0;
  assign sign_d = 1'b0;
  assign sign_dp = 1'b0;
  assign sign_e = 1'b0;
  assign sign_f = 1'b0;
  assign sign_g = in3;

  // Notes on the sheet:
  //   Interface (do not edit the content inside this box)
  //   Outputs:
  //   Inputs
  //   Sign
  //   Decimal Number
endmodule

/* Test case:
in3 in2 in1 in0  sign_a sign_b sign_c sign_d sign_e sign_f sign_g  seg_a seg_b seg_c seg_d seg_e seg_f seg_g
 0   0   0   0    0      0      0      0      0      0      0       1     1     1     1     1     1     0
*/
